# Fritzing sketch I2C_esp8266NodeMCUToArduinoUno (saved by Fritzing 0.8.5b)

parts:
  U1 = NodeMCU V1.0
  Part1 = Arduino Uno (Rev3) - ICSP

nets:
  N1: U1.D3, Part1.A4/SDA
  N2: U1.D4, Part1.A5/SCL

notes:
  NodeMCU (D3) -> UNO (A4)
  NodeMCU (D4) -> UNO (A5)

custom parts:
  NodeMCU V1.0: ESP8266 based NodeMCU
